// Logisim project exp6-1b.circ as structural Verilog: 1 circuit, main circuit main
module main (
  input  [2:0] ABC,
  output F
);

  wire decoder_1_out0, decoder_1_out2, decoder_1_out3, decoder_1_out6;

  Decoder #(.select(3), .tristate("false")) decoder_1 (
    .out0(decoder_1_out0), .out2(decoder_1_out2), .out3(decoder_1_out3), .out6(decoder_1_out6), .sel(ABC));  // open: out1, out4, out5, out7
  or or_1 (F, decoder_1_out0, decoder_1_out2, decoder_1_out3, decoder_1_out6);

  // Notes on the sheet:
  //   Erikson Sodergren
  //   section 1, experiment 6
  //   activity 1b, due april 12
endmodule
