// Logisim project exp6-1c.circ as structural Verilog: 1 circuit, main circuit main
module main (
  input  [2:0] ABC,
  output F
);

  Multiplexer #(.select(3), .width(1)) multiplexer_1 (
    .in0(1'b1), .in1(1'b0), .in2(1'b1), .in3(1'b1), .in4(1'b1), .in5(1'b0), .in6(1'b1), .in7(1'b0), .out(F),
    .sel(ABC));

  // Notes on the sheet:
  //   Erikson Sodergren
  //   section 1, experiment 6
  //   activity 1c, due april 12
endmodule
