// Logisim project exp6-2a.circ as structural Verilog: 1 circuit, main circuit main
module main (
);

  wire and_1_out, and_2_out, bcd_to_7_segment_decoder_1_p4, bcd_to_7_segment_decoder_1_p5,
       bcd_to_7_segment_decoder_1_p6, bcd_to_7_segment_decoder_1_p7, bcd_to_7_segment_decoder_1_p8,
       bcd_to_7_segment_decoder_1_p9, bcd_to_7_segment_decoder_1_p10, bcd_to_7_segment_decoder_1_p11,
       CLK_out, CLR_out, j_k_ff_1_q, j_k_ff_2_q, j_k_ff_3_q;

  Button CLK (.out(CLK_out));
  Button CLR (.out(CLR_out));
  J_K_Flip_Flop #(.trigger("rising")) j_k_ff_1 (
    .J(1'b1), .clk(CLK_out), .K(1'b1), .Q(j_k_ff_1_q), .reset(CLR_out));  // open: Qn, preset, en
  J_K_Flip_Flop #(.trigger("rising")) j_k_ff_2 (
    .J(j_k_ff_1_q), .clk(CLK_out), .K(j_k_ff_1_q), .Q(j_k_ff_2_q), .reset(CLR_out));  // open: Qn, preset, en
  and and_1 (and_1_out, j_k_ff_1_q, j_k_ff_2_q);
  J_K_Flip_Flop #(.trigger("rising")) j_k_ff_3 (
    .J(and_1_out), .clk(CLK_out), .K(and_1_out), .Q(j_k_ff_3_q), .reset(CLR_out));  // open: Qn, preset, en
  and and_2 (and_2_out, and_1_out, j_k_ff_3_q);
  // BCD_to_7_segment_decoder bcd_to_7_segment_decoder_1: pin names not known; wires that end beside it: j_k_ff_1_q, j_k_ff_2_q, j_k_ff_3_q, bcd_to_7_segment_decoder_1_p4, bcd_to_7_segment_decoder_1_p5, bcd_to_7_segment_decoder_1_p6, bcd_to_7_segment_decoder_1_p7, bcd_to_7_segment_decoder_1_p8, bcd_to_7_segment_decoder_1_p9, bcd_to_7_segment_decoder_1_p10, bcd_to_7_segment_decoder_1_p11
  J_K_Flip_Flop #(.trigger("rising")) j_k_ff_4 (
    .J(and_2_out), .clk(CLK_out), .K(and_2_out), .Q(bcd_to_7_segment_decoder_1_p4), .reset(CLR_out));  // open: Qn, preset, en
  _7_Segment_Display u_7_segment_display_1 (
    .g(bcd_to_7_segment_decoder_1_p11), .f(bcd_to_7_segment_decoder_1_p10),
    .a(bcd_to_7_segment_decoder_1_p5), .b(bcd_to_7_segment_decoder_1_p6), .e(bcd_to_7_segment_decoder_1_p9),
    .d(bcd_to_7_segment_decoder_1_p8), .c(bcd_to_7_segment_decoder_1_p7));  // open: dp

  // Notes on the sheet:
  //   Erikson Sodergren
  //   section 1, experiment 6
  //   activity 2a, due april 12
endmodule
