// Logisim project exp6-2b.circ as structural Verilog: 1 circuit, main circuit main
module main (
);

  wire bcd_to_7_segment_decoder_1_p5, bcd_to_7_segment_decoder_1_p6, bcd_to_7_segment_decoder_1_p7,
       bcd_to_7_segment_decoder_1_p8, bcd_to_7_segment_decoder_1_p9, bcd_to_7_segment_decoder_1_p10,
       bcd_to_7_segment_decoder_1_p11, CLK_out, CLR_out, j_k_ff_1_q, j_k_ff_2_q, j_k_ff_3_q, j_k_ff_4_q,
       nor_1_out, nor_2_out, not_1_out, not_2_out;

  J_K_Flip_Flop #(.trigger("rising")) j_k_ff_1 (
    .J(1'b1), .clk(CLK_out), .K(1'b1), .Q(j_k_ff_1_q), .reset(CLR_out));  // open: Qn, preset, en
  Button CLK (.out(CLK_out));
  not not_1 (not_1_out, j_k_ff_1_q);
  Button CLR (.out(CLR_out));
  J_K_Flip_Flop #(.trigger("rising")) j_k_ff_2 (
    .J(not_1_out), .clk(CLK_out), .K(not_1_out), .Q(j_k_ff_2_q), .reset(CLR_out));  // open: Qn, preset, en
  nor nor_1 (nor_1_out, j_k_ff_1_q, j_k_ff_2_q);
  J_K_Flip_Flop #(.trigger("rising")) j_k_ff_3 (
    .J(nor_1_out), .clk(CLK_out), .K(nor_1_out), .Q(j_k_ff_3_q), .reset(CLR_out));  // open: Qn, preset, en
  not not_2 (not_2_out, nor_1_out);
  nor nor_2 (nor_2_out, not_2_out, j_k_ff_3_q);
  J_K_Flip_Flop #(.trigger("rising")) j_k_ff_4 (
    .J(nor_2_out), .clk(CLK_out), .K(nor_2_out), .Q(j_k_ff_4_q), .reset(CLR_out));  // open: Qn, preset, en
  // BCD_to_7_segment_decoder bcd_to_7_segment_decoder_1: pin names not known; wires that end beside it: j_k_ff_1_q, j_k_ff_2_q, j_k_ff_3_q, j_k_ff_4_q, bcd_to_7_segment_decoder_1_p5, bcd_to_7_segment_decoder_1_p6, bcd_to_7_segment_decoder_1_p7, bcd_to_7_segment_decoder_1_p8, bcd_to_7_segment_decoder_1_p9, bcd_to_7_segment_decoder_1_p10, bcd_to_7_segment_decoder_1_p11
  _7_Segment_Display u_7_segment_display_1 (
    .g(bcd_to_7_segment_decoder_1_p11), .f(bcd_to_7_segment_decoder_1_p10),
    .a(bcd_to_7_segment_decoder_1_p5), .b(bcd_to_7_segment_decoder_1_p6), .e(bcd_to_7_segment_decoder_1_p9),
    .d(bcd_to_7_segment_decoder_1_p8), .c(bcd_to_7_segment_decoder_1_p7));  // open: dp

  // Notes on the sheet:
  //   Erikson Sodergren
  //   section 1, experiment 6
  //   activity 2b, due april 12
endmodule
